# Fritzing sketch Arduino GSM-Control-Circuit (saved by Fritzing 0.8.3b)
breadboards: 1

parts:
  Device = Screw terminal - 2 pins [package=THT]
  R7 = Resistor [tolerance=±5% resistance=330 package=THT]
  Relay = Relay [package=THT]
  Transistor = NPN-Transistor [part_number=BC546 package="TO92 [THT]"]
  Diode = Rectifier Diode [part_number=1N4007 package="300 mil [THT]"]
  R8 = Resistor [resistance=1k tolerance=±5% package=THT]
  Power = Power plug
  LED = LED - 5mm [color="Red (633nm)" package="5 mm [THT]"]

nets:
  N1: Device.pin1, Relay.B
  N2: Device.pin2, Power.GND
  N3: R7.Pin_0, LED.cathode
  N4: R7.Pin_1, Relay.COIL1, Transistor.C, Diode.anode
  N5: Relay.C1, Relay.C2, Power.VCC
  5V: Relay.COIL2, Diode.cathode, LED.anode
  GND: Transistor.E
  N6: Transistor.B, R8.Pin_0
