# Fritzing sketch Arduino GSM (saved by Fritzing 0.8.3b)
circuit board: 6.9215cm x 5.33756cm
breadboards: 1

parts:
  Relay_1 = Relay [package=THT]
  Power_1 = Power plug
  R3 = Resistor [resistance=1k tolerance=±5% package=THT]
  Transistor_1 = NPN-Transistor [part_number=BC546 package="TO92 [THT]"]
  Diode_1 = Rectifier Diode [part_number=1N4007 package="300 mil [THT]"]
  Arduino1 = Arduino
  LED1 = LED - 5mm [color="Red (633nm)" package="5 mm [THT]"]
  Device_1 = Screw terminal - 2 pins [package=THT]
  Relay_2 = Relay [package=THT]
  Transistor_2 = NPN-Transistor [part_number=BC546 package="TO92 [THT]"]
  Diode_2 = Rectifier Diode [part_number=1N4007 package="300 mil [THT]"]
  R4 = Resistor [resistance=1k tolerance=±5% package=THT]
  Power_2 = Power plug
  LED2 = LED - 5mm [color="Red (633nm)" package="5 mm [THT]"]
  Device_2 = Screw terminal - 2 pins [package=THT]
  R6 = Resistor [tolerance=±5% resistance=330 package=THT]
  R5 = Resistor [tolerance=±5% resistance=220 package=THT]
  U2 = mystery part, 3 pins [chip_label=GSM]

nets (from the schematic view):
  N1: Relay_1.COIL1, Transistor_1.C, Diode_1.anode, R5.Pin_1
  N2: Relay_1.C1, Relay_1.C2, Power_1.VCC
  N3: Relay_1.COIL2, Diode_1.cathode, Arduino1.+5V, LED1.anode, Relay_2.COIL2, Diode_2.cathode, LED2.anode
  N4: Relay_1.B, Device_1.pin1
  N5: Power_1.GND, Device_1.pin2
  N6: R3.Pin_0, Transistor_1.B
  N7: R3.Pin_1, Arduino1.D10
  N8: Transistor_1.E, Arduino1.GND, Transistor_2.E
  N9: Arduino1.D11, R4.Pin_1
  N10: Arduino1.D7, U2.pin1
  N11: Arduino1.D3, U2.pin2
  N12: Arduino1.D2, U2.pin3
  N13: LED1.cathode, R5.Pin_0
  N14: Relay_2.COIL1, Transistor_2.C, Diode_2.anode, R6.Pin_1
  N15: Relay_2.C1, Relay_2.C2, Power_2.VCC
  N16: Relay_2.B, Device_2.pin1
  N17: Transistor_2.B, R4.Pin_0
  N18: Power_2.GND, Device_2.pin2
  N19: LED2.cathode, R6.Pin_0

notes:
  GSM / GPRS Shield Module
